# Fritzing sketch Wiring (saved by Fritzing 0.9.3b)
breadboards: 1

parts:
  Part1 = Arduino Mega 2560 (Rev3)
  Part2 = LCD1602-I2C
  S1 = KY-026
  J1 = Basic Servo
  Part3 = Thumb Joystick
  Part4 = RFID-RC522-v2  # not connected

nets:
  N1: Part1.A0, S1.pin1
  N2: Part1.A1, Part3.VERT
  N3: Part1.A2, Part3.HORZ
  N4: Part1.SCL, Part2.SCL
  N5: Part1.SDA, Part2.SDA
  GND: Part1.GND, Part2.GND
  VIN: Part1.VIN, Part2.VCC
  N6: Part1.D2_PWM, J1.pulse
  N7: Part1.D3_PWM, Part3.SEL
  N8: Part1.D22, S1.pin4
  GND_2: S1.pin2, J1.gnd, Part3.GND
  VCC: S1.pin3, J1.vcc, Part3.VCC

custom parts:
  LCD1602-I2C: A standard character display, usually with 2x16 characters. Comes in many colors with LCM1602 IIC attached.
  KY-026: ky-026 flame sensor module
  RFID-RC522-v2: A simple China made RFID-RC522 Reader; do check the pin labels, as this is a MFRC522 based clone.
